# Fritzing sketch iot-device-schema (saved by Fritzing 0.9.5d)
breadboards: 1

parts:
  Raspberry_Pi_2 = Raspberry Pi 3 [part_number=RPI-3-V1.2]
  Part1 = LCD1602-I2C
  Mod1 = KY-004 Key Switch Module [package="Breakout board"]
  LED3 = smd LED [color="Green (555nm)" package="0603 [SMD]"]
  LED4 = smd LED [color="Red (633nm)" package="0603 [SMD]"]
  R1 = Resistor [tolerance=±5% resistance=220 package=THT]
  R2 = Resistor [tolerance=±5% resistance=220 package=THT]

nets:
  N1: Raspberry_Pi_2.GPIO2, Part1.SDA
  N2: Raspberry_Pi_2.GPIO3, Part1.SCL
  GND: Raspberry_Pi_2.GND, Part1.GND, Mod1.-, LED3.cathode, LED4.cathode
  N3: Raspberry_Pi_2.GIPO24, R2.Pin_0
  N4: Raspberry_Pi_2.GIPO23, R1.Pin_0
  N5: Raspberry_Pi_2.GIPO18, Mod1.S
  5V: Raspberry_Pi_2.5V, Part1.VCC, Mod1.Vin
  N6: LED3.anode, R1.Pin_1
  N7: LED4.anode, R2.Pin_1

custom parts:
  LCD1602-I2C: A standard character display, usually with 2x16 characters. Comes in many colors with LCM1602 IIC attached.
  KY-004 Key Switch Module: Arduino Key Switch Module Keyes KY-004 is a push button that will output a high signal when pressed.
